# Fritzing sketch CircuitDiagram (saved by Fritzing 0.9.3b)
breadboards: 1

parts:
  Part1 = Arduino Nano (Rev3.0)
  U1 = POT [package=alps_pot]
  U2 = POT [package=alps_pot]
  S1 = Pushbutton [package="[THT]"]
  S2 = Pushbutton [package="[THT]"]
  S3 = Pushbutton [package="[THT]"]
  R1 = Resistor [tolerance=±5% resistance=10k package=THT]
  R2 = Resistor [tolerance=±5% resistance=10k package=THT]
  R3 = Resistor [tolerance=±5% resistance=10k package=THT]
  Part2 = Ludus ProtoShield
  VCC1 = Battery
  VCC2 = Battery
  J1 = Basic Servo
  J2 = Basic Servo
  J3 = Basic Servo
  LED11 = LED - 5mm [color="White (6500K)" package="5 mm [THT]"]
  LED12 = LED - 5mm [color="White (6500K)" package="5 mm [THT]"]
  LED1 = LED - 5mm [color="White (6500K)" package="5 mm [THT]"]
  LED2 = LED - 5mm [color="White (6500K)" package="5 mm [THT]"]
  R5 = Resistor [tolerance=±5% resistance=22 package="1206 [SMD]"]
  LED3 = LED - 5mm [color="White (6500K)" package="5 mm [THT]"]
  LED9 = LED - 5mm [color="White (6500K)" package="5 mm [THT]"]
  LED7 = LED - 5mm [color="White (6500K)" package="5 mm [THT]"]
  R7 = Resistor [tolerance=±5% resistance=22 package="1206 [SMD]"]
  LED8 = LED - 5mm [color="White (6500K)" package="5 mm [THT]"]
  LED4 = LED - 5mm [color="White (6500K)" package="5 mm [THT]"]
  R9 = Resistor [tolerance=±5% resistance=22 package="1206 [SMD]"]
  R8 = Resistor [tolerance=±5% resistance=22 package="1206 [SMD]"]
  R6 = Resistor [tolerance=±5% resistance=22 package="1206 [SMD]"]
  LED5 = LED - 5mm [color="White (6500K)" package="5 mm [THT]"]
  LED10 = LED - 5mm [color="White (6500K)" package="5 mm [THT]"]
  R4 = Resistor [tolerance=±5% resistance=22 package="1206 [SMD]"]
  LED6 = LED - 5mm [color="White (6500K)" package="5 mm [THT]"]
  LED13 = LED - 5mm [color="Red (633nm)" package="5 mm [THT]"]
  LED14 = LED - 5mm [color="Red (633nm)" package="5 mm [THT]"]
  LED15 = LED - 5mm [color="Red (633nm)" package="5 mm [THT]"]
  R10 = Resistor [tolerance=±5% resistance=220 package=THT]
  R11 = Resistor [tolerance=±5% resistance=220 package=THT]
  R12 = Resistor [tolerance=±5% resistance=220 package=THT]
  S4 = Pushbutton [package="[THT]"]
  R13 = Resistor [tolerance=±5% resistance=10k package=THT]

nets:
  N1: Part1.D2, S1.Pin_1, S1.Pin_2, R3.Pin_1
  N2: Part1.D3, S2.Pin_1, S2.Pin_2, R2.Pin_1
  N3: Part1.D4, S3.Pin_1, S3.Pin_2, R1.Pin_1
  N4: Part1.D5, S4.Pin_1, S4.Pin_2, R13.Pin_1
  N5: Part1.D8, LED15.anode
  N6: Part1.D9, LED14.anode
  N7: Part1.D10, LED13.anode
  GND: Part1.GND, U1.E, U2.E, R1.Pin_0, R2.Pin_0, R3.Pin_0, Part2.GND, J1.gnd, J2.gnd, J3.gnd, R10.Pin_1, R11.Pin_1, R12.Pin_1, R13.Pin_0
  5V: Part1.5V, U1.A, U2.A, S1.Pin_3, S1.Pin_4, S2.Pin_3, S2.Pin_4, S3.Pin_3, S3.Pin_4, Part2.VCC, S4.Pin_3, S4.Pin_4
  N8: Part1.A5, Part2.SCL
  N9: Part1.A4, Part2.SDA
  N10: Part1.A1, U1.S
  N11: Part1.A0, U2.S
  VCC: Part2.ANALOG_PWR_RAIL, J1.vcc, J2.vcc, J3.vcc
  N12: Part2.A0, J1.pulse
  N13: Part2.A1, J2.pulse
  N14: Part2.A2, J3.pulse
  N15: Part2.AOUT2, VCC1.-
  N16: Part2.AOUT1, VCC2.+
  N17: VCC1.+, VCC2.-
  N18: LED11.cathode, R9.Pin_0
  N19: LED11.anode, LED12.cathode
  N20: LED12.anode, LED2.anode, LED8.anode, LED4.anode, LED10.anode, LED6.anode
  N21: LED1.cathode, R4.Pin_0
  N22: LED1.anode, LED2.cathode
  N23: R5.Pin_0, LED3.cathode
  N24: R5.Pin_1, R7.Pin_1, R9.Pin_1, R8.Pin_1, R6.Pin_1, R4.Pin_1
  N25: LED3.anode, LED4.cathode
  N26: LED9.cathode, R8.Pin_0
  N27: LED9.anode, LED10.cathode
  N28: LED7.cathode, R6.Pin_0
  N29: LED7.anode, LED8.cathode
  N30: R7.Pin_0, LED5.cathode
  N31: LED5.anode, LED6.cathode

notes:
  light, switch
  cont
  light
  save, load
  pretend this is PCA9685 16-Channel Servo Driver
  6v ~2000mAh
  5v 300mA
  6*22ohm
  mode leds
